# Fritzing sketch Scheme (saved by Fritzing 0.9.3b)

parts:
  Part1 = Arduino Nano (Rev3.0)
  U3 = RELAY [package=relay-t9a]
  U4 = RELAY [package=relay-t9a]
  U5 = RELAY [package=relay-t9a]
  U6 = RELAY [package=relay-t9a]
  LCD1 = LCD screen
  R1 = Resistor [tolerance=±5% resistance=220 package="2512 [SMD]"]
  S1 = Round Pushbutton
  R2 = Resistor [tolerance=±5% resistance=10k package="2512 [SMD]"]

nets:
  GND: Part1.GND, U3.COIL1, U6.COIL1, LCD1.VSS, LCD1.V0, LCD1.R/W, LCD1.LED-, R2.Pin_1
  N1: Part1.D2, LCD1.DB7
  N2: Part1.D3, LCD1.DB6
  N3: Part1.D4, LCD1.DB5
  N4: Part1.D5, LCD1.DB4
  N5: Part1.D6, LCD1.RS
  N6: Part1.D7, LCD1.E
  N7: Part1.D10, S1.leg1, R2.Pin_0
  dirPin: Part1.D11/MOSI
  pulPin: Part1.D12/MISO
  5V: Part1.5V, LCD1.VDD, R1.Pin_0, S1.leg0
  N8: Part1.A3, U6.COIL2
  N9: Part1.A2, U5.COIL2
  N10: Part1.A1, U4.COIL2
  N11: Part1.A0, U3.COIL2
